// Logisim project alu-control.circ as structural Verilog: 1 circuit, main circuit main
module main (
  input  [5:0] Instruction_5_0,
  input  [3:0] ALUOp,
  output [3:0] ALUSwitch
);


  assign ALUSwitch = 4'b0000;
endmodule
