// Logisim project alu.circ as structural Verilog: 2 circuits, main circuit main
module main (
  input  [31:0] X,
  input  [31:0] Y,
  input  [3:0] Switch,
  output Signed_Overflow,
  output Equal,
  output [31:0] Result
);

  wire and_2_out, and_3_out, and_4_out, and_5_out, and_6_out, comparator_1_lt, comparator_2_lt, not_1_out,
       not_2_out, not_3_out, not_4_out, not_5_out, not_6_out, OF_minus, or_2_out;
  wire [31:0] ADD, AND, OR, SLL, SLT, SLTU, SRA, SRL, SUB;

  Comparator #(.width(32)) comparator_1 (.a(X), .b(Y), .lt(comparator_1_lt));  // open: gt, eq
  Comparator #(.width(32), .mode("unsigned")) comparator_2 (.a(X), .b(Y), .lt(comparator_2_lt));  // open: gt, eq
  Shifter #(.width(32)) shifter_1 (.in(Y), .\dist (X[4:0]), .out(SLL));
  Shifter #(.width(32), .shift("lr")) shifter_2 (.in(Y), .\dist (X[4:0]), .out(SRL));
  Shifter #(.width(32), .shift("ar")) shifter_3 (.in(Y), .\dist (X[4:0]), .out(SRA));
  assign SLT = {{31{1'b0}}, comparator_1_lt};  // Bit_Extender bit_extender_1
  assign SLTU = {{31{1'b0}}, comparator_2_lt};  // Bit_Extender bit_extender_2
  Adder #(.width(32)) adder_1 (.a(X), .b(Y), .out(ADD));  // open: cin, cout
  Subtractor #(.width(32)) subtractor_1 (.a(X), .b(Y), .out(SUB), .bout(OF_minus));  // open: bin
  assign AND = X & Y;  // AND_Gate and_1, 32 bits wide
  assign OR = X | Y;  // OR_Gate or_1, 32 bits wide
  Multiplexer #(.select(4), .width(32), .enable("false")) multiplexer_1 (
    .in0(SLL), .in1(SRL), .in2(SRA), .in5(ADD), .in6(ADD), .in7(SUB), .in8(SUB), .in9(AND), .in10(OR),
    .in14(SLT), .in15(SLTU), .out(Result), .sel(Switch));  // open: in3, in4, in11, in12, in13
  not not_1 (not_1_out, ADD[31]);
  not not_2 (not_2_out, X[31]);
  not not_3 (not_3_out, Y[31]);
  not not_4 (not_4_out, Switch[3]);
  not not_5 (not_5_out, Switch[1]);
  and and_2 (and_2_out, X[31], Y[31], not_1_out);
  and and_3 (and_3_out, not_2_out, ADD[31], not_3_out);
  not not_6 (not_6_out, Switch[3]);
  and and_4 (and_4_out, not_4_out, Switch[2], not_5_out, Switch[0]);
  or or_2 (or_2_out, and_2_out, and_3_out);
  and and_5 (and_5_out, not_6_out, Switch[2], OF_minus, Switch[1], Switch[0]);
  and and_6 (and_6_out, and_4_out, or_2_out);
  isEqual isEqual (.X(X), .Y(Y), .isEqual(Equal));
  or or_3 (Signed_Overflow, and_6_out, and_5_out);

  // Other names for the same wires on the sheet: ADDU[31:0] = ADD; overflow = Signed_Overflow; S[3:0] = Switch;
  //   SUBU[31:0] = SUB

  // Notes on the sheet:
  //   INPUTS to your circuit
  //   SHIFTING
  //   LESS THAN
  //   DON'T CHANGE THE LOCATIONS OF THE INPUTS AND OUTPUTS!
  //   OPERANDS AND LOGIC
  //   OUTPUTS from your circuit
  //   OVERFLOW AND EQUAL
endmodule

module isEqual (
  input  [31:0] X,
  input  [31:0] Y,
  output isEqual
);

  wire or_1_out;
  wire [31:0] xor_1_out;

  assign xor_1_out = X ^ Y;  // XOR_Gate xor_1, 32 bits wide
  or or_1 (or_1_out, xor_1_out[0], xor_1_out[1], xor_1_out[2], xor_1_out[3], xor_1_out[4], xor_1_out[5], xor_1_out[6], xor_1_out[7], xor_1_out[8], xor_1_out[9], xor_1_out[10], xor_1_out[11], xor_1_out[12], xor_1_out[13], xor_1_out[14], xor_1_out[15], xor_1_out[17], xor_1_out[18], xor_1_out[19], xor_1_out[20], xor_1_out[21], xor_1_out[22], xor_1_out[23], xor_1_out[24], xor_1_out[25], xor_1_out[26], xor_1_out[27], xor_1_out[28], xor_1_out[29], xor_1_out[30], xor_1_out[31], xor_1_out[16]);
  not not_1 (isEqual, or_1_out);
endmodule
