// Logisim project control.circ as structural Verilog: 1 circuit, main circuit main
module main (
  input  [5:0] instruction_31_26,
  output [1:0] RegDst,
  output Jump,
  output Branch,
  output MemRead,
  output MemtoReg,
  output [3:0] ALUOp,
  output MemWrite,
  output ALUSrc,
  output RegWrite,
  output JAL
);

  wire comparator_2_eq, comparator_6_eq, comparator_7_eq, comparator_8_eq, IsAdd, IsAddU, isAnd, isJ, IsLUI,
       IsLW, isOr, isSLT, isSLTU, or_5_out, xor_1_out;

  Comparator #(.width(6)) comparator_1 (.a(instruction_31_26), .b({6{1'b0}}), .eq(RegDst[0]));  // open: gt, lt
  Comparator #(.width(6)) comparator_2 (.a(instruction_31_26), .b(6'b001000), .eq(comparator_2_eq));  // open: gt, lt
  Comparator #(.width(6)) comparator_3 (.a(instruction_31_26), .b(6'b001111), .eq(IsLUI));  // open: gt, lt
  Comparator #(.width(6)) comparator_4 (.a(instruction_31_26), .b(6'b100011), .eq(IsLW));  // open: gt, lt
  Comparator #(.width(6)) comparator_5 (.a(instruction_31_26), .b(6'b101011), .eq(MemWrite));  // open: gt, lt
  Comparator #(.width(6)) comparator_6 (.a(instruction_31_26), .b(6'b000100), .eq(comparator_6_eq));  // open: gt, lt
  or or_1 (Branch, comparator_6_eq, comparator_7_eq, comparator_8_eq);
  Comparator #(.width(6)) comparator_7 (.a(instruction_31_26), .b(6'b000101), .eq(comparator_7_eq));  // open: gt, lt
  Comparator #(.width(6)) comparator_8 (.a(instruction_31_26), .b(6'b000001), .eq(comparator_8_eq));  // open: gt, lt
  Comparator #(.width(6)) comparator_9 (.a(instruction_31_26), .b(6'b001001), .eq(IsAddU));  // open: gt, lt
  Comparator #(.width(6)) comparator_10 (.a(instruction_31_26), .b(6'b001100), .eq(isAnd));  // open: gt, lt
  Comparator #(.width(6)) comparator_11 (.a(instruction_31_26), .b(6'b001101), .eq(isOr));  // open: gt, lt
  Comparator #(.width(6)) comparator_12 (.a(instruction_31_26), .b(6'b001010), .eq(isSLT));  // open: gt, lt
  Comparator #(.width(6)) comparator_13 (.a(instruction_31_26), .b(6'b001011), .eq(isSLTU));  // open: gt, lt
  Comparator #(.width(6)) comparator_14 (.a(instruction_31_26), .b(6'b000011), .eq(JAL));  // open: gt, lt
  Comparator #(.width(6)) comparator_15 (.a(instruction_31_26), .b(6'b000010), .eq(isJ));  // open: gt, lt
  or or_2 (MemRead, IsLW, IsLUI);
  or or_3 (IsAdd, comparator_2_eq, IsLW, MemWrite);
  or or_4 (Jump, isJ, JAL);
  or Op0 (ALUOp[0], isSLTU, isAnd, IsLUI, IsAdd, Branch);
  nor Op1 (ALUOp[1], RegDst[0], IsAdd, IsLUI, isAnd);
  nor Op1_2 (ALUOp[2], IsLUI, RegDst[0], isOr, isAnd);
  or Op3 (ALUOp[3], isAnd, isOr, isSLT, isSLTU);
  not not_1 (MemtoReg, IsLW);
  or or_5 (or_5_out, IsLUI, xor_1_out);
  xor xor_1 (xor_1_out, IsAdd, MemWrite);
  nor nor_1 (ALUSrc, Branch, RegDst[0]);
  or or_6 (RegWrite, RegDst[0], IsAddU, isSLT, isSLTU, isAnd, isOr, or_5_out, JAL);

  assign RegDst[1] = JAL;

  // Other names for the same wires on the sheet: Input[5:0] = instruction_31_26; IsALUSrc = ALUSrc; IsJump = Jump;
  //   IsLoad = MemRead; IsMemRead = MemRead; IsMemToReg = MemtoReg; IsRegWrite = RegWrite; IsBranch = Branch;
  //   IsSub = Branch; IsSW_MemWrite = MemWrite; IsR = RegDst[0]; IsRegDest = RegDst[0]; isJAL = JAL;
  //   TheOp[3:0] = ALUOp

  // Notes on the sheet:
  //   Determine Instruction Type
  //   ALUOp
  //   The MemToReg MUX is flipped
  //   NOSING IS DONE WITH THIS
endmodule
